// Logisim project 8-bit MPU.circ as structural Verilog: 8 circuits, main circuit main
module main (
  input  [7:0] Emulation_Din,
  input  Test,
  input  Test_2,
  input  [3:0] Emulation_Adr,
  output [3:0] MAR_Content,
  output [3:0] Counter_content,
  output [7:0] IR_Content,
  output [7:0] MBR_Content,
  output [7:0] Reg_A_Content,
  output [7:0] out_10,
  output [2:0] content_of_step_counter,
  output [7:0] ALU_Result,
  output [7:0] Reg_B_Content
);

  wire C0, C1, C2, C3, C4, C5, C6, C7, C8, C9, C10, C11, C12, C13, C14, C15, CLK;
  wire [3:0] bitselector_2_out, controlled_buffer_1_out, Deci_deco_4_out_2_2, MAR_dout;
  wire [7:0] ALU_dout, bit_extender_1_out, bit_extender_2_out, Instruction_Reg_dout;
  wire [31:0] Deci_deco_2_out_2, Deci_deco_3_out_2, Deci_deco_4_out_2, Deci_deco_5_out_2, Deci_deco_out_2;

  _8_bits_Register Register_A (.Clock(CLK), .WE(C12), .Din(ALU_dout), .Stored_Data(Reg_A_Content));  // open: OE, Dout
  _8_bits_Register Register_B (.Clock(CLK), .WE(C13), .Din(ALU_dout), .Stored_Data(Reg_B_Content));  // open: OE, Dout
  Counter #(.width(4), .max('h3)) counter_1 (
    .D(controlled_buffer_1_out), .count(C1), .Q(Counter_content), .clk(CLK));  // open: load, carry, clr
  _8_bits_Register Instruction_Reg (
    .Clock(CLK), .WE(C7), .Din(ALU_dout), .OE(C8), .Dout(Instruction_Reg_dout), .Stored_Data(IR_Content));
  _7_Segment_Display u_7_segment_display_1 (
    .g(Deci_deco_out_2[15]), .f(Deci_deco_out_2[14]), .a(Deci_deco_out_2[13]), .b(Deci_deco_out_2[12]),
    .e(Deci_deco_out_2[31]), .d(Deci_deco_out_2[30]), .c(Deci_deco_out_2[29]), .dp(Deci_deco_out_2[28]));
  Decimal_Decoder Deci_deco (.in_1(Reg_A_Content), .out_2(Deci_deco_out_2));
  ALU ALU (
    .Reg_A(Reg_A_Content), .Reg_B(Reg_B_Content), .OE(C11), .Dout(ALU_dout), .ALU_Result(ALU_Result));  // open: Carry_out
  Decimal_Decoder Deci_deco_2 (.in_1(Reg_B_Content), .out_2(Deci_deco_2_out_2));
  assign controlled_buffer_1_out = C0 ? Counter_content : 4'bz;  // Controlled_Buffer controlled_buffer_1
  _7_Segment_Display u_7_segment_display_2 (
    .g(Deci_deco_out_2[7]), .f(Deci_deco_out_2[6]), .a(Deci_deco_out_2[5]), .b(Deci_deco_out_2[4]),
    .e(Deci_deco_out_2[23]), .d(Deci_deco_out_2[22]), .c(Deci_deco_out_2[21]), .dp(Deci_deco_out_2[20]));
  _7_Segment_Display u_7_segment_display_3 (
    .g(Deci_deco_out_2[11]), .f(Deci_deco_out_2[10]), .a(Deci_deco_out_2[9]), .b(Deci_deco_out_2[8]),
    .e(Deci_deco_out_2[27]), .d(Deci_deco_out_2[26]), .c(Deci_deco_out_2[25]), .dp(Deci_deco_out_2[24]));
  _7_Segment_Display u_7_segment_display_4 (
    .g(Deci_deco_2_out_2[11]), .f(Deci_deco_2_out_2[10]), .a(Deci_deco_2_out_2[9]), .b(Deci_deco_2_out_2[8]),
    .e(Deci_deco_2_out_2[27]), .d(Deci_deco_2_out_2[26]), .c(Deci_deco_2_out_2[25]),
    .dp(Deci_deco_2_out_2[24]));
  _7_Segment_Display u_7_segment_display_5 (
    .g(Deci_deco_2_out_2[15]), .f(Deci_deco_2_out_2[14]), .a(Deci_deco_2_out_2[13]),
    .b(Deci_deco_2_out_2[12]), .e(Deci_deco_2_out_2[31]), .d(Deci_deco_2_out_2[30]),
    .c(Deci_deco_2_out_2[29]), .dp(Deci_deco_2_out_2[28]));
  _7_Segment_Display u_7_segment_display_6 (
    .g(Deci_deco_out_2[3]), .f(Deci_deco_out_2[2]), .a(Deci_deco_out_2[1]), .b(Deci_deco_out_2[0]),
    .e(Deci_deco_out_2[19]), .d(Deci_deco_out_2[18]), .c(Deci_deco_out_2[17]), .dp(Deci_deco_out_2[16]));
  _7_Segment_Display u_7_segment_display_7 (
    .g(Deci_deco_2_out_2[3]), .f(Deci_deco_2_out_2[2]), .a(Deci_deco_2_out_2[1]), .b(Deci_deco_2_out_2[0]),
    .e(Deci_deco_2_out_2[19]), .d(Deci_deco_2_out_2[18]), .c(Deci_deco_2_out_2[17]),
    .dp(Deci_deco_2_out_2[16]));
  _7_Segment_Display u_7_segment_display_8 (
    .g(Deci_deco_2_out_2[7]), .f(Deci_deco_2_out_2[6]), .a(Deci_deco_2_out_2[5]), .b(Deci_deco_2_out_2[4]),
    .e(Deci_deco_2_out_2[23]), .d(Deci_deco_2_out_2[22]), .c(Deci_deco_2_out_2[21]),
    .dp(Deci_deco_2_out_2[20]));
  BitSelector #(.group(4)) bitselector_1 (.in(Instruction_Reg_dout), .out(controlled_buffer_1_out), .sel(1'b0));
  LED D7 (.in(ALU_dout[7]));
  assign bit_extender_1_out = {{4{1'b0}}, Counter_content};  // Bit_Extender bit_extender_1
  assign ALU_dout = Test ? Emulation_Din : 8'bz;  // Controlled_Buffer controlled_buffer_2
  LED D4 (.in(ALU_dout[4]));
  LED D6 (.in(ALU_dout[6]));
  LED D5 (.in(ALU_dout[5]));
  _7_Segment_Display u_7_segment_display_9 (
    .g(Deci_deco_3_out_2[3]), .f(Deci_deco_3_out_2[2]), .a(Deci_deco_3_out_2[1]), .b(Deci_deco_3_out_2[0]),
    .e(Deci_deco_3_out_2[19]), .d(Deci_deco_3_out_2[18]), .c(Deci_deco_3_out_2[17]),
    .dp(Deci_deco_3_out_2[16]));
  Decimal_Decoder Deci_deco_3 (.in_1(bit_extender_1_out), .out_2(Deci_deco_3_out_2));
  LED D3 (.in(ALU_dout[3]));
  LED D1 (.in(ALU_dout[1]));
  LED D0 (.in(ALU_dout[0]));
  LED D2 (.in(ALU_dout[2]));
  assign ALU_dout = C5 ? MBR_Content : 8'bz;  // Controlled_Buffer controlled_buffer_3
  Decimal_Decoder Deci_deco_4 (
    .in_1(out_10), .out_2({Deci_deco_4_out_2[31:20], Deci_deco_4_out_2_2, Deci_deco_4_out_2[15:0]}));
  MAR MAR (.Clock(CLK), .WE(C9), .Din(controlled_buffer_1_out), .OE(C10), .Dout(MAR_dout), .Stored_Data(MAR_Content));
  _8_bits_Register MBR (.Clock(CLK), .WE(C4), .Din(ALU_dout), .OE(C6), .Dout(ALU_dout), .Stored_Data(MBR_Content));
  _8_bits_Register Output_Reg (.Clock(CLK), .WE(C15), .Din(ALU_dout), .OE(C14), .Dout(ALU_dout), .Stored_Data(out_10));
  _7_Segment_Display u_7_segment_display_10 (
    .g(Deci_deco_4_out_2[11]), .f(Deci_deco_4_out_2[10]), .a(Deci_deco_4_out_2[9]), .b(Deci_deco_4_out_2[8]),
    .e(Deci_deco_4_out_2[27]), .d(Deci_deco_4_out_2[26]), .c(Deci_deco_4_out_2[25]),
    .dp(Deci_deco_4_out_2[24]));
  _7_Segment_Display u_7_segment_display_11 (
    .g(Deci_deco_4_out_2[15]), .f(Deci_deco_4_out_2[14]), .a(Deci_deco_4_out_2[13]),
    .b(Deci_deco_4_out_2[12]), .e(Deci_deco_4_out_2[31]), .d(Deci_deco_4_out_2[30]),
    .c(Deci_deco_4_out_2[29]), .dp(Deci_deco_4_out_2[28]));
  assign MAR_dout = Test_2 ? Emulation_Adr : 4'bz;  // Controlled_Buffer controlled_buffer_4
  _7_Segment_Display u_7_segment_display_12 (
    .g(Deci_deco_4_out_2[7]), .f(Deci_deco_4_out_2[6]), .a(Deci_deco_4_out_2[5]), .b(Deci_deco_4_out_2[4]),
    .e(Deci_deco_4_out_2[23]), .d(Deci_deco_4_out_2[22]), .c(Deci_deco_4_out_2[21]),
    .dp(Deci_deco_4_out_2[20]));
  _7_Segment_Display u_7_segment_display_13 (
    .g(Deci_deco_4_out_2[3]), .f(Deci_deco_4_out_2[2]), .a(Deci_deco_4_out_2[1]), .b(Deci_deco_4_out_2[0]),
    .e(Deci_deco_4_out_2_2[3]), .d(Deci_deco_4_out_2_2[2]), .c(Deci_deco_4_out_2_2[1]),
    .dp(Deci_deco_4_out_2_2[0]));
  LED D7_2 (.in(ALU_dout[7]));
  LED D6_2 (.in(ALU_dout[6]));
  LED D4_2 (.in(ALU_dout[4]));
  LED D3_2 (.in(ALU_dout[3]));
  LED D2_2 (.in(ALU_dout[2]));
  LED D5_2 (.in(ALU_dout[5]));
  LED D0_2 (.in(ALU_dout[0]));
  LED D1_2 (.in(ALU_dout[1]));
  BitSelector #(.group(4)) bitselector_2 (.in(IR_Content), .out(bitselector_2_out), .sel(1'b1));
  Clock Clock (.out(CLK));
  RAM #(.addrWidth(4), .bus("separate")) ram_1 (
    .addr(MAR_dout), .din(ALU_dout), .data(ALU_dout), .str(C2), .clk(CLK), .ld(C3));  // open: sel, clr
  Counter #(.width(3), .max('h5)) counter_2 (
    .Q(content_of_step_counter), .clk(CLK));  // open: load, D, count, carry, clr
  assign bit_extender_2_out = {{5{1'b0}}, content_of_step_counter};  // Bit_Extender bit_extender_2
  Decimal_Decoder Deci_deco_5 (.in_1(bit_extender_2_out), .out_2(Deci_deco_5_out_2));
  CU_I cu_i_1 (
    .OPC3(bitselector_2_out[3]), .OPC2(bitselector_2_out[2]), .OPC1(bitselector_2_out[1]),
    .OPC0(bitselector_2_out[0]), .SC2(content_of_step_counter[2]), .SC1(content_of_step_counter[1]),
    .SC0(content_of_step_counter[0]), .C0(C0), .C1(C1), .C2(C2), .C3(C3), .C4(C4), .C5(C5), .C6(C6), .C7(C7),
    .C8(C8), .C9(C9), .C10(C10), .C11(C11));
  CU_II cu_ii_1 (
    .OPC3(bitselector_2_out[3]), .OPC2(bitselector_2_out[2]), .OPC1(bitselector_2_out[1]),
    .OPC0(bitselector_2_out[0]), .SC2(content_of_step_counter[2]), .SC1(content_of_step_counter[1]),
    .SC0(content_of_step_counter[0]), .C12(C12), .C13(C13), .C14(C14), .C15(C15));
  _7_Segment_Display u_7_segment_display_14 (
    .g(Deci_deco_5_out_2[3]), .f(Deci_deco_5_out_2[2]), .a(Deci_deco_5_out_2[1]), .b(Deci_deco_5_out_2[0]),
    .e(Deci_deco_5_out_2[19]), .d(Deci_deco_5_out_2[18]), .c(Deci_deco_5_out_2[17]),
    .dp(Deci_deco_5_out_2[16]));
  LED led_1 (.in(C0));
  LED led_2 (.in(C1));
  LED led_3 (.in(C2));
  LED led_4 (.in(C3));
  LED led_5 (.in(C4));
  LED led_6 (.in(C5));
  LED led_7 (.in(C6));
  LED led_8 (.in(C7));
  LED led_9 (.in(C8));
  LED led_10 (.in(C9));
  LED led_11 (.in(C10));
  LED led_12 (.in(C11));
  LED led_13 (.in(C12));
  LED led_14 (.in(C13));
  LED led_15 (.in(C14));
  LED led_16 (.in(C15));

  // Notes on the sheet:
  //   Program Counter
  //   Internal Data Bus (8 bits)
  //   Internal Address Bus (4 bits)
  //   External Data Bus (8 bits)
  //   RAM
endmodule

module _1bit_memory_cell (
  input  Clock,
  input  WE,
  input  Din,
  input  OE,
  input  RESET,
  output Dout,
  output Stored_Data
);

  wire and_1_out, and_2_out, not_1_out, or_1_out;

  not not_1 (not_1_out, WE);
  and and_1 (and_1_out, Stored_Data, not_1_out);
  and and_2 (and_2_out, WE, Din);
  or or_1 (or_1_out, and_1_out, and_2_out);
  D_Flip_Flop d_ff_1 (.clk(Clock), .D(or_1_out), .Q(Stored_Data), .reset(RESET));  // open: Qn, preset, en
  assign Dout = OE ? Stored_Data : 1'bz;  // Controlled_Buffer controlled_buffer_1

  // Notes on the sheet:
  //   1 BIT MEMORY CELL
endmodule

module _8_bits_Register (
  input  Clock,
  input  WE,
  input  [7:0] Din,
  input  OE,
  output [7:0] Dout,
  output [7:0] Stored_Data
);

  _1bit_memory_cell D0 (
    .Clock(Clock), .WE(WE), .Din(Din[0]), .OE(OE), .Dout(Dout[0]), .Stored_Data(Stored_Data[0]));  // open: RESET
  _1bit_memory_cell D1 (
    .Clock(Clock), .WE(WE), .Din(Din[1]), .OE(OE), .Dout(Dout[1]), .Stored_Data(Stored_Data[1]));  // open: RESET
  _1bit_memory_cell D2 (
    .Clock(Clock), .WE(WE), .Din(Din[2]), .OE(OE), .Dout(Dout[2]), .Stored_Data(Stored_Data[2]));  // open: RESET
  _1bit_memory_cell D3 (
    .Clock(Clock), .WE(WE), .Din(Din[3]), .OE(OE), .Dout(Dout[3]), .Stored_Data(Stored_Data[3]));  // open: RESET
  _1bit_memory_cell D4 (
    .Clock(Clock), .WE(WE), .Din(Din[4]), .OE(OE), .Dout(Dout[4]), .Stored_Data(Stored_Data[4]));  // open: RESET
  _1bit_memory_cell D5 (
    .Clock(Clock), .WE(WE), .Din(Din[5]), .OE(OE), .Dout(Dout[5]), .Stored_Data(Stored_Data[5]));  // open: RESET
  _1bit_memory_cell D6 (
    .Clock(Clock), .WE(WE), .Din(Din[6]), .OE(OE), .Dout(Dout[6]), .Stored_Data(Stored_Data[6]));  // open: RESET
  _1bit_memory_cell D7 (
    .Clock(Clock), .WE(WE), .Din(Din[7]), .OE(OE), .Dout(Dout[7]), .Stored_Data(Stored_Data[7]));  // open: RESET

  // Notes on the sheet:
  //   8-bits Register
endmodule

module MAR (
  input  Clock,
  input  WE,
  input  [3:0] Din,
  input  OE,
  output [3:0] Dout,
  output [3:0] Stored_Data
);

  _1bit_memory_cell D0 (
    .Clock(Clock), .WE(WE), .Din(Din[0]), .OE(OE), .Dout(Dout[0]), .Stored_Data(Stored_Data[0]));  // open: RESET
  _1bit_memory_cell D1 (
    .Clock(Clock), .WE(WE), .Din(Din[1]), .OE(OE), .Dout(Dout[1]), .Stored_Data(Stored_Data[1]));  // open: RESET
  _1bit_memory_cell D2 (
    .Clock(Clock), .WE(WE), .Din(Din[2]), .OE(OE), .Dout(Dout[2]), .Stored_Data(Stored_Data[2]));  // open: RESET
  _1bit_memory_cell D3 (
    .Clock(Clock), .WE(WE), .Din(Din[3]), .OE(OE), .Dout(Dout[3]), .Stored_Data(Stored_Data[3]));  // open: RESET

  // Notes on the sheet:
  //   MAR
endmodule

module ALU (
  input  [7:0] Reg_A,
  input  [7:0] Reg_B,
  input  OE,
  output [7:0] Dout,
  output [7:0] ALU_Result,
  output Carry_out
);

  Adder adder_1 (.a(Reg_A), .b(Reg_B), .out(ALU_Result), .cout(Carry_out));  // open: cin
  assign Dout = OE ? ALU_Result : 8'bz;  // Controlled_Buffer controlled_buffer_1

  // Notes on the sheet:
  //   Arithmetic Logic Unit
  //   ALU
endmodule

module Decimal_Decoder (
  input  [7:0] in_1,
  output [31:0] out_2
);

  ROM #(.dataWidth(32)) rom_1 (
    .addr(in_1),
    .data({out_2[31:28], out_2[15:12], out_2[27:24], out_2[11:8], out_2[23:20], out_2[7:4], out_2[19:16], out_2[3:0]}));  // open: sel

  // Notes on the sheet:
  //   contents of rom_1 (hex, n*v repeats v):
  //   e7 21 cb 6b 2d 6e ee 23 ef 2f 21e7 2121 21cb 216b 212d 216e 21ee 2123 21ef 212f cbe7 cb21 cbcb cb6b
  //   cb2d cb6e cbee cb23 cbef cb2f 6be7 6b21 6bcb 6b6b 6b2d 6b6e 6bee 6b23 6bef 6b2f 2de7 2d21 2dcb 2d6b
  //   2d2d 2d6e 2dee 2d23 2def 2d2f 6ee7 6e21 6ecb 6e6b 6e2d 6e6e 6eee 6e23 6eef 6e2f eee7 ee21 eecb ee6b
  //   ee2d ee6e eeee ee23 eeef ee2f 23e7 2321 23cb 236b 232d 236e 23ee 2323 23ef 232f efe7 ef21 efcb ef6b
  //   ef2d ef6e efee ef23 efef ef2f 2fe7 2f21 2fcb 2f6b 2f2d 2f6e 2fee 2f23 2fef 2f2f 21e7e7 21e721 21e7cb
  //   21e76b 21e72d 21e76e 21e7ee 21e723 21e7ef 21e72f 2121e7 212121 2121cb 21216b 21212d 21216e 2121ee
  //   212123 2121ef 21212f 21cbe7 21cb21 21cbcb 21cb6b 21cb2d 21cb6e 21cbee 21cb23 21cbef 21cb2f 216be7
  //   216b21 216bcb 216b6b 216b2d 216b6e 216bee 216b23 216bef 216b2f 212de7 212d21 212dcb 212d6b 212d2d
  //   212d6e 212dee 212d23 212def 212d2f 216ee7 216e21 216ecb 216e6b 216e2d 216e6e 216eee 216e23 216eef
  //   216e2f 21eee7 21ee21 21eecb 21ee6b 21ee2d 21ee6e 21eeee 21ee23 21eeef 21ee2f 2123e7 212321 2123cb
  //   21236b 21232d 21236e 2123ee 212323 2123ef 21232f 21efe7 21ef21 21efcb 21ef6b 21ef2d 21ef6e 21efee
  //   21ef23 21efef 21ef2f 212fe7 212f21 212fcb 212f6b 212f2d 212f6e 212fee 212f23 212fef 212f2f cbe7e7
  //   cbe721 cbe7cb cbe76b cbe72d cbe76e cbe7ee cbe723 cbe7ef cbe72f cb21e7 cb2121 cb21cb cb216b cb212d
  //   cb216e cb21ee cb2123 cb21ef cb212f cbcbe7 cbcb21 cbcbcb cbcb6b cbcb2d cbcb6e cbcbee cbcb23 cbcbef
  //   cbcb2f cb6be7 cb6b21 cb6bcb cb6b6b cb6b2d cb6b6e cb6bee cb6b23 cb6bef cb6b2f cb2de7 cb2d21 cb2dcb
  //   cb2d6b cb2d2d cb2d6e cb2dee cb2d23 cb2def cb2d2f cb6ee7 cb6e21 cb6ecb cb6e6b cb6e2d cb6e6e
  //   Decimal Decoder
endmodule

module CU_I (
  input  OPC3,
  input  OPC2,
  input  OPC1,
  input  OPC0,
  input  SC2,
  input  SC1,
  input  SC0,
  output C0,
  output C1,
  output C2,
  output C3,
  output C4,
  output C5,
  output C6,
  output C7,
  output C8,
  output C9,
  output C10,
  output C11
);

  wire and_1_out, and_2_out, and_3_out, and_4_out, and_5_out, and_6_out, and_8_out, and_9_out, and_10_out,
       and_11_out, and_12_out, and_13_out, and_14_out, and_17_out, and_18_out, and_19_out, and_20_out,
       and_21_out, and_22_out, and_23_out, and_24_out, and_25_out, and_26_out, and_27_out, and_28_out,
       and_29_out, and_30_out, not_1_out, not_2_out, not_3_out, not_4_out, not_5_out, not_6_out, not_7_out,
       not_8_out, not_9_out, not_10_out, not_11_out, not_12_out, not_13_out, not_14_out, not_15_out,
       not_16_out, not_17_out, not_18_out, not_19_out, not_20_out, not_21_out, not_22_out, not_23_out,
       not_24_out, not_25_out, not_26_out, not_27_out, not_28_out, not_29_out, not_30_out, not_31_out,
       not_32_out, not_33_out, not_34_out, not_35_out, not_36_out, not_37_out, not_38_out, not_39_out,
       not_40_out, not_41_out, not_42_out, not_43_out, not_44_out, not_45_out, not_46_out, not_47_out,
       not_48_out, not_49_out, not_50_out, not_51_out, not_52_out, not_53_out, not_54_out, not_55_out,
       not_56_out, not_57_out, not_58_out, not_59_out, not_60_out, not_61_out, not_62_out, not_63_out,
       not_64_out, not_65_out, not_66_out, not_67_out, not_68_out, not_69_out, not_70_out, not_71_out,
       not_72_out, not_73_out, not_74_out, not_75_out, not_76_out, not_77_out, not_78_out;

  not not_1 (not_1_out, OPC3);
  not not_2 (not_2_out, OPC2);
  not not_3 (not_3_out, SC2);
  not not_4 (not_4_out, SC1);
  not not_5 (not_5_out, SC0);
  not not_6 (not_6_out, OPC2);
  not not_7 (not_7_out, OPC1);
  not not_8 (not_8_out, SC2);
  not not_9 (not_9_out, SC1);
  not not_10 (not_10_out, SC0);
  not not_11 (not_11_out, OPC1);
  not not_12 (not_12_out, OPC0);
  not not_13 (not_13_out, SC2);
  not not_14 (not_14_out, SC1);
  not not_15 (not_15_out, SC0);
  not not_16 (not_16_out, SC2);
  not not_17 (not_17_out, SC1);
  not not_18 (not_18_out, SC2);
  not not_19 (not_19_out, SC1);
  not not_20 (not_20_out, SC2);
  not not_21 (not_21_out, SC1);
  not not_22 (not_22_out, SC1);
  not not_23 (not_23_out, SC0);
  not not_24 (not_24_out, SC2);
  not not_25 (not_25_out, SC1);
  not not_26 (not_26_out, OPC1);
  not not_27 (not_27_out, SC1);
  not not_28 (not_28_out, SC0);
  not not_29 (not_29_out, SC2);
  not not_30 (not_30_out, SC1);
  not not_31 (not_31_out, OPC1);
  not not_32 (not_32_out, SC1);
  not not_33 (not_33_out, SC0);
  not not_34 (not_34_out, SC2);
  not not_35 (not_35_out, SC2);
  not not_36 (not_36_out, SC0);
  not not_37 (not_37_out, OPC1);
  not not_38 (not_38_out, SC1);
  not not_39 (not_39_out, SC1);
  not not_40 (not_40_out, SC0);
  not not_41 (not_41_out, OPC3);
  not not_42 (not_42_out, OPC2);
  not not_43 (not_43_out, SC2);
  not not_44 (not_44_out, SC0);
  not not_45 (not_45_out, OPC1);
  not not_46 (not_46_out, SC2);
  not not_47 (not_47_out, SC2);
  not not_48 (not_48_out, OPC2);
  not not_49 (not_49_out, SC2);
  not not_50 (not_50_out, SC1);
  not not_51 (not_51_out, SC0);
  not not_52 (not_52_out, OPC1);
  not not_53 (not_53_out, SC2);
  not not_54 (not_54_out, SC2);
  not not_55 (not_55_out, SC1);
  not not_56 (not_56_out, SC0);
  not not_57 (not_57_out, SC2);
  not not_58 (not_58_out, SC2);
  not not_59 (not_59_out, SC1);
  not not_60 (not_60_out, SC0);
  not not_61 (not_61_out, SC2);
  not not_62 (not_62_out, SC1);
  not not_63 (not_63_out, SC0);
  not not_64 (not_64_out, SC2);
  not not_65 (not_65_out, SC1);
  not not_66 (not_66_out, OPC1);
  not not_67 (not_67_out, SC1);
  not not_68 (not_68_out, SC0);
  not not_69 (not_69_out, SC1);
  not not_70 (not_70_out, SC0);
  not not_71 (not_71_out, OPC0);
  not not_72 (not_72_out, SC2);
  not not_73 (not_73_out, OPC0);
  not not_74 (not_74_out, SC1);
  not not_75 (not_75_out, SC0);
  not not_76 (not_76_out, OPC0);
  not not_77 (not_77_out, SC1);
  not not_78 (not_78_out, SC0);
  and and_1 (and_1_out, not_1_out, not_2_out, not_3_out, not_4_out, not_5_out);
  and and_2 (and_2_out, not_6_out, not_7_out, not_8_out, not_9_out, not_10_out);
  and and_3 (and_3_out, OPC3, not_11_out, not_12_out, not_13_out, not_14_out, not_15_out);
  and and_4 (and_4_out, not_16_out, not_17_out, SC0);
  and and_5 (and_5_out, OPC2, OPC1, not_18_out, not_19_out);
  and and_6 (and_6_out, OPC3, OPC1, not_20_out, not_21_out);
  and and_7 (C2, OPC1, OPC0, SC2, not_22_out, not_23_out);
  and and_8 (and_8_out, not_24_out, not_25_out, SC0);
  and and_9 (and_9_out, not_26_out, SC2, not_27_out, not_28_out);
  and and_10 (and_10_out, not_29_out, not_30_out, SC0);
  and and_11 (and_11_out, not_31_out, SC2, not_32_out, not_33_out);
  and and_12 (and_12_out, OPC1, OPC0, not_34_out, SC0);
  and and_13 (and_13_out, not_35_out, SC1, not_36_out);
  and and_14 (and_14_out, not_37_out, SC2, not_38_out, SC0);
  and and_15 (C6, OPC1, OPC0, SC2, not_39_out, not_40_out);
  and and_16 (C7, not_41_out, not_42_out, not_43_out, SC1, not_44_out);
  and and_17 (and_17_out, not_45_out, not_46_out, SC1, SC0);
  and and_18 (and_18_out, OPC0, not_47_out, SC1, SC0);
  and and_19 (and_19_out, not_48_out, not_49_out, not_50_out, not_51_out);
  and and_20 (and_20_out, not_52_out, not_53_out, SC1, SC0);
  and and_21 (and_21_out, OPC0, not_54_out, not_55_out, not_56_out);
  and and_22 (and_22_out, OPC0, not_57_out, SC1, SC0);
  and and_23 (and_23_out, OPC1, not_58_out, not_59_out, not_60_out);
  and and_24 (and_24_out, OPC3, not_61_out, not_62_out, not_63_out);
  and and_25 (and_25_out, not_64_out, not_65_out, SC0);
  and and_26 (and_26_out, not_66_out, SC2, not_67_out, not_68_out);
  and and_27 (and_27_out, OPC0, SC2, not_69_out, not_70_out);
  and and_28 (and_28_out, OPC1, not_71_out, not_72_out, SC1, SC0);
  and and_29 (and_29_out, OPC2, OPC1, not_73_out, SC2, not_74_out, not_75_out);
  and and_30 (and_30_out, OPC3, OPC1, not_76_out, SC2, not_77_out, not_78_out);
  or or_1 (C0, and_1_out, and_2_out, and_3_out);
  or or_2 (C1, and_4_out, and_5_out, and_6_out);
  or or_3 (C3, and_8_out, and_9_out);
  or or_4 (C4, and_10_out, and_11_out, and_12_out);
  or or_5 (C5, and_13_out, and_14_out);
  or or_6 (C8, and_17_out, and_18_out);
  or or_7 (C9, and_19_out, and_20_out, and_21_out, and_22_out, and_23_out, and_24_out);
  or or_8 (C10, and_25_out, and_26_out, and_27_out);
  or or_9 (C11, and_28_out, and_29_out, and_30_out);
endmodule

module CU_II (
  input  OPC3,
  input  OPC2,
  input  OPC1,
  input  OPC0,
  input  SC2,
  input  SC1,
  input  SC0,
  output C12,
  output C13,
  output C14,
  output C15
);

  wire not_1_out, not_2_out, not_3_out, not_4_out, not_5_out, not_6_out, not_7_out, not_8_out;

  not not_1 (not_1_out, OPC1);
  not not_2 (not_2_out, OPC0);
  not not_3 (not_3_out, SC1);
  not not_4 (not_4_out, OPC1);
  not not_5 (not_5_out, SC1);
  not not_6 (not_6_out, SC2);
  not not_7 (not_7_out, OPC0);
  not not_8 (not_8_out, SC2);
  and and_1 (C12, not_1_out, not_2_out, SC2, not_3_out, SC0);
  and and_2 (C13, not_4_out, OPC0, SC2, not_5_out, SC0);
  and and_3 (C14, OPC1, OPC0, not_6_out, SC1, SC0);
  and and_4 (C15, OPC1, not_7_out, not_8_out, SC1, SC0);
endmodule
